# Fritzing sketch turtle sketch (saved by Fritzing 1.0.1rc)
breadboards: 1

parts:
  Mod1 = Raspberry Pi 4B
  J1 = Basic Servo
  J2 = Basic Servo
  S4 = Pushbutton [package="[THT]"]
  J3 = Piezo Speaker
  R1 = Resistor [tolerance=±5% power=0.25W resistance=220 package=THT]

nets:
  VCC: Mod1.5V, J1.vcc, J2.vcc, R1.Pin_1
  GND: Mod1.GND, J1.gnd, J2.gnd, S4.Pin_1, S4.Pin_2, J3.pin1
  N1: Mod1.GPIO14, J2.pulse
  N2: Mod1.GPIO18, J1.pulse
  N3: Mod1.GPIO23, J3.pin2
  N4: Mod1.GPIO20, S4.Pin_3, S4.Pin_4, R1.Pin_0
